// Digital circuit part3.dig as structural Verilog
module part3 (
  input  s_0,
  input  s_1,
  input  s_2,
  output \output 
);

  wire decoder_1_out_2, decoder_1_out_3, decoder_1_out_6, or_1_out, or_2_out, or_3_out;

  Decoder #(.Selector_Bits(3)) decoder_1 (
    .sel({s_2, s_1, s_0}), .out_2(decoder_1_out_2), .out_3(decoder_1_out_3), .out_6(decoder_1_out_6));  // open: out_0, out_1, out_4, out_5, out_7
  or or_1 (or_1_out, decoder_1_out_2, decoder_1_out_3);
  or or_2 (or_2_out, decoder_1_out_3, decoder_1_out_6);
  or or_3 (or_3_out, or_1_out, or_2_out);
  nor nor_1 (\output , or_3_out, 1'b0);
endmodule
