// Digital circuit ZeroToSixtyCounter2Hz.dig as structural Verilog
module ZeroToSixtyCounter2Hz (
  input  _2_Hz
);

  wire and_1_out, cntdecud_1_p6, d_ff_1_nq, d_ff_1_q, nand_1_out, not_1_out, not_2_out;
  wire [3:0] cntdecud_1_p5, cntdecud_2_p5;

  D_FF d_ff_1 (.D(d_ff_1_nq), .C(_2_Hz), .Q(d_ff_1_q), .nQ(d_ff_1_nq));
  nand nand_1 (nand_1_out, not_2_out, cntdecud_2_p5[1], cntdecud_2_p5[2], not_1_out);
  and and_1 (and_1_out, cntdecud_1_p6, 1'b1);
  // cntDECud cntdecud_1: pin names not known; wires that end beside it: 1'b1, 1'b0, d_ff_1_q, nand_1_out, cntdecud_1_p5, cntdecud_1_p6
  // cntDECud cntdecud_2: pin names not known; wires that end beside it: and_1_out, 1'b0, d_ff_1_q, nand_1_out, cntdecud_2_p5
  not not_1 (not_1_out, cntdecud_2_p5[3]);
  not not_2 (not_2_out, cntdecud_2_p5[0]);
  Seven_Seg_Hex seven_seg_hex_1 (.d(cntdecud_2_p5), .dp(1'b0));
  Seven_Seg_Hex seven_seg_hex_2 (.d(cntdecud_1_p5), .dp(1'b0));

  // Notes on the sheet:
  //   _2_Hz: Hz: 2
  //   In order to increase the time it takes, 
  //   we can use a D flip flop to double the time,
  //   knowing that f = 1/t
  //   Kourosh Sharifi
  //   30438
  //   The max number we want is 60.
  //   We care about the 6 on the left for the limiter.
  //   Hence we say:
  //   (6)_10 = (0110)_2
  //   Hence we have to reverse the 0-th and 3rd bits.
endmodule
