// Digital circuit cntBCD.dig as structural Verilog
module cntBCD (
  input  CLK,
  output [3:0] CNT
);

  wire and_1_out, and_2_out, and_3_out, and_4_out, and_5_out, and_6_out, and_7_out, d_ff_1_nq, d_ff_2_nq,
       d_ff_3_nq, d_ff_4_nq, multiplexer_1_out, multiplexer_2_out, multiplexer_3_out, not_1_out;

  and and_1 (and_1_out, CNT[0], CNT[3]);
  not not_1 (not_1_out, and_1_out);
  and and_2 (and_2_out, d_ff_1_nq, not_1_out);
  and and_3 (and_3_out, multiplexer_1_out, not_1_out);
  and and_4 (and_4_out, multiplexer_2_out, not_1_out);
  and and_5 (and_5_out, multiplexer_3_out, not_1_out);
  D_FF d_ff_1 (.D(and_2_out), .C(CLK), .Q(CNT[0]), .nQ(d_ff_1_nq));
  D_FF d_ff_2 (.D(and_3_out), .C(CLK), .Q(CNT[1]), .nQ(d_ff_2_nq));
  D_FF d_ff_3 (.D(and_4_out), .C(CLK), .Q(CNT[2]), .nQ(d_ff_3_nq));
  D_FF d_ff_4 (.D(and_5_out), .C(CLK), .Q(CNT[3]), .nQ(d_ff_4_nq));
  Multiplexer multiplexer_1 (.sel(CNT[0]), .in_0(CNT[1]), .in_1(d_ff_2_nq), .out(multiplexer_1_out));
  Multiplexer multiplexer_2 (.sel(and_6_out), .in_0(CNT[2]), .in_1(d_ff_3_nq), .out(multiplexer_2_out));
  Multiplexer multiplexer_3 (.sel(and_7_out), .in_0(CNT[3]), .in_1(d_ff_4_nq), .out(multiplexer_3_out));
  and and_6 (and_6_out, CNT[0], CNT[1]);
  and and_7 (and_7_out, CNT[2], and_6_out);

  // Notes on the sheet:
  //   9_{10} = 1001_{2}
  //   If you take the
  //   (out_0 AND out_3)
  //   When they are both 1,
  //   you'll get 9,
  //   or the reset funciton.
endmodule
