// Digital circuit lab1_main.dig as structural Verilog
module lab1_main (
  input  in_1,
  input  in_2,
  input  in_3,
  input  in_4,
  input  in_5,
  input  in_6,
  input  in_7,
  input  in_8
);

  wire add_1_c_o, add_2_c_o;
  wire [3:0] unsignedbcd6_1_p1, unsignedbcd6_1_p3, unsignedbcd_1_p1, unsignedbcd_1_p3, unsignedbcd_2_p1,
       unsignedbcd_2_p3;
  wire [5:0] add_1_s, add_2_s;

  Seven_Seg_Hex seven_seg_hex_1 (.d(unsignedbcd_1_p1), .dp(1'b0));
  Seven_Seg_Hex seven_seg_hex_2 (.d(unsignedbcd_1_p3), .dp(1'b0));
  // unsignedBCD unsignedbcd_1: pin names not known; wires that end beside it: unsignedbcd_1_p1, {in_5, in_6, in_7, in_8}, unsignedbcd_1_p3
  Add #(.Bits(6)) add_1 (
    .a({2'b00, in_5, in_6, in_7, in_8}), .b({2'b00, in_5, in_6, in_7, in_8}), .c_i(1'b0), .s(add_1_s),
    .c_o(add_1_c_o));
  Seven_Seg_Hex seven_seg_hex_3 (.d(unsignedbcd_2_p1), .dp(1'b0));
  Seven_Seg_Hex seven_seg_hex_4 (.d(unsignedbcd_2_p3), .dp(1'b0));
  // unsignedBCD unsignedbcd_2: pin names not known; wires that end beside it: unsignedbcd_2_p1, {in_1, in_2, in_3, in_4}, unsignedbcd_2_p3
  Seven_Seg_Hex seven_seg_hex_5 (.d(unsignedbcd6_1_p1), .dp(1'b0));
  Seven_Seg_Hex seven_seg_hex_6 (.d(unsignedbcd6_1_p3), .dp(1'b0));
  Add #(.Bits(6)) add_2 (
    .a({2'b00, in_1, in_2, in_3, in_4}), .b(add_1_s), .c_i(add_1_c_o), .s(add_2_s), .c_o(add_2_c_o));
  // unsignedBCD6 unsignedbcd6_1: pin names not known; wires that end beside it: unsignedbcd6_1_p1, add_2_s, unsignedbcd6_1_p3
  // also tied to GND on the sheet: add_2_c_o

  // Notes on the sheet:
  //   Kourosh Sharifi
  //   30438
  //   [a_3, a_2, a_1, a_0]
  //   = [0, 0, a_3, a_2, a_1, a_0]
  //   2x
  //   2 \times  A = A + A
  //   +
  //   =
endmodule
