// Digital circuit prelab4.dig as structural Verilog
module prelab4 (
  input  clk,
  input  RST
);

  wire and_1_out, and_2_out, and_3_out, and_4_out, cntdecud_1_p6, cntdecud_1_p7, d_ff_1_nq, d_ff_2_nq,
       DOWN_out, UP_out;
  wire [3:0] cntdecud_1_p5, cntdecud_2_p5;

  Button UP (.out(UP_out));
  D_FF d_ff_1 (.D(UP_out), .C(clk), .nQ(d_ff_1_nq));  // open: Q
  and and_1 (and_1_out, UP_out, d_ff_1_nq);
  Button DOWN (.out(DOWN_out));
  D_FF d_ff_2 (.D(DOWN_out), .C(clk), .nQ(d_ff_2_nq));  // open: Q
  and and_2 (and_2_out, DOWN_out, d_ff_2_nq);
  // cntDECud cntdecud_1: pin names not known; wires that end beside it: and_1_out, and_2_out, clk, RST, cntdecud_1_p5, cntdecud_1_p6, cntdecud_1_p7
  and and_3 (and_3_out, cntdecud_1_p7, and_1_out);
  and and_4 (and_4_out, cntdecud_1_p6, and_2_out);
  // cntDECud cntdecud_2: pin names not known; wires that end beside it: and_3_out, and_4_out, clk, RST, cntdecud_2_p5
  Seven_Seg_Hex seven_seg_hex_1 (.d(cntdecud_2_p5), .dp(1'b0));
  Seven_Seg_Hex seven_seg_hex_2 (.d(cntdecud_1_p5), .dp(1'b0));

  // Notes on the sheet:
  //   clk: Hz: 100
  //   Once the simulation starts, the 'RST' button must be pressed.
  //   Thereafter, by pressing the 'UP' button, the counter increases, starting from 00.
  //   If 'DOWN' is pressed, the counter decreases.
  //   Once it reaches 99, then it will go to 00.
  //   Components used:
  //   • two push buttons
  //   • two seven-segment hex displays (with the dot inputs grounded)
  //   • a real time clock running at 100 Hz
  //   • a 1-bit input to control the reset inputs of counters
endmodule
