// Digital circuit prelab_02.dig as structural Verilog
module prelab_02 (
  input  MSB__A,
  input  B,
  input  C,
  input  LSB__D
);

  wire and_1_out, and_2_out, and_3_out, and_4_out, and_5_out, and_6_out, not_1_out, not_2_out, not_3_out,
       not_4_out, or_1_out, or_2_out, or_3_out;

  not not_1 (not_1_out, MSB__A);
  not not_2 (not_2_out, B);
  not not_3 (not_3_out, C);
  not not_4 (not_4_out, LSB__D);
  and and_1 (and_1_out, MSB__A, not_2_out);
  and and_2 (and_2_out, not_1_out, B);
  and and_3 (and_3_out, B, not_3_out);
  and and_4 (and_4_out, not_2_out, C);
  and and_5 (and_5_out, C, not_4_out);
  and and_6 (and_6_out, not_3_out, LSB__D);
  or or_1 (or_1_out, and_1_out, and_2_out);
  or or_2 (or_2_out, and_3_out, and_4_out);
  or or_3 (or_3_out, and_5_out, and_6_out);
  LED X__MSB (.in(MSB__A));
  LED Y (.in(or_1_out));
  LED Z (.in(or_2_out));
  LED T__LSB (.in(or_3_out));
endmodule
