// Digital circuit unsignedBCD6.dig as structural Verilog
module unsignedBCD6 (
  input  [5:0] Input,
  output [3:0] tens,
  output [3:0] units
);

  wire add3_1_p4, add3_1_p6, add3_2_p1, add3_2_p3, add3_2_p6, add3_2_p9, add3_2_p12, add3_4_p1, add3_4_p3,
       add3_5_p1, add3_5_p4;

  // add3 add3_1: pin names not known; wires that end beside it: 1'b0, 1'b0, 1'b0, add3_1_p4, add3_1_p4, add3_1_p6, add3_1_p6
  // add3 add3_2: pin names not known; wires that end beside it: add3_2_p1, add3_2_p1, add3_2_p3, add3_2_p3, tens[3], add3_2_p6, add3_2_p6, tens[2], add3_2_p9, add3_2_p9, tens[1], add3_2_p12, add3_2_p12, tens[0]
  // add3 add3_3: pin names not known; wires that end beside it: 1'b0, Input[5], Input[4], Input[3]
  // add3 add3_4: pin names not known; wires that end beside it: add3_4_p1, add3_4_p1, add3_4_p3, add3_4_p3, Input[2]
  // add3 add3_5: pin names not known; wires that end beside it: add3_5_p1, add3_5_p1, units[3], add3_5_p4, add3_5_p4, units[2], Input[1], units[1]
  // Pins of 4 and 6 bits meet at Input

  assign units[0] = Input[0];
endmodule
