// Digital circuit part1.dig as structural Verilog
module part1 (
  input  s_0,
  input  s_1,
  input  s_2,
  output d_0,
  output d_1,
  output d_2,
  output d_3,
  output d_4,
  output d_5,
  output d_6,
  output d_7
);

  wire not_1_out;

  not not_1 (not_1_out, s_2);
  Demultiplexer #(.Selector_Bits(2)) demultiplexer_1 (
    .sel({s_1, s_0}), .in(not_1_out), .out_0(d_0), .out_1(d_1), .out_2(d_2), .out_3(d_3));
  Demultiplexer #(.Selector_Bits(2)) demultiplexer_2 (
    .sel({s_1, s_0}), .in(s_2), .out_0(d_4), .out_1(d_5), .out_2(d_6), .out_3(d_7));
endmodule
