// Digital circuit part4.dig as structural Verilog
module part4 (
  input  a,
  input  b,
  input  c_in,
  output s,
  output c_out
);

  wire not_1_out;

  Multiplexer #(.Selector_Bits(2)) multiplexer_1 (
    .sel({b, a}), .in_0(c_in), .in_1(not_1_out), .in_2(not_1_out), .in_3(c_in), .out(s));
  not not_1 (not_1_out, c_in);
  Multiplexer #(.Selector_Bits(2)) multiplexer_2 (
    .sel({b, a}), .in_0(a), .in_1(c_in), .in_2(c_in), .in_3(a), .out(c_out));
endmodule
