// Digital circuit hw01_core.dig as structural Verilog
module hw01_core (
  input  A0,
  input  A1,
  input  B0,
  input  B1,
  output [3:0] M
);

  wire [1:0] and_1_out;
  wire [2:1] and_2_out;

  and and_1 (and_1_out[0], A0, B0);
  and and_2 (and_2_out[1], A1, B0);
  and and_3 (and_1_out[1], A0, B1);
  and and_4 (and_2_out[2], A1, B1);
  Add #(.Bits(3)) add_1 (.a({1'b0, and_1_out}), .b({and_2_out, 1'b0}), .c_i(1'b0), .s(M[2:0]), .c_o(M[3]));

  // Notes on the sheet:
  //   [A_1 , A_0]
  //   [B_1 , B_0]
  //   A_0 \wedge B_0 = C_0
  //   A_1 \wedge B_0 = C_2
  //   A_0 \times  B_0
  //   A_0 \wedge B_1 = C_1
  //   A_1 \times  B_0
  //   A_1 \wedge B_1 = C_3
  //   A_0 \times  B_1
  //   A_1 \times  B_1
  //   [0 , C_1 , C_0]
  //   [C_3 , C_2 , 0]
  //   Kourosh Sharifi
  //   [0, C_1, C_0]
  //   +
  //   [C_3 , C_2 , 0]
  //   =
  //   [carry_2, C_3 + carry_1, C_2 + C_1, C_0]
  //   =
  //   [2^3, 2^2, 2^1, 2^0]
endmodule
